// Logisim project Control_unit.circ as structural Verilog: 3 circuits, main circuit ctrl_unit
module ctrl_unit (
  input  [3:0] in_1,
  output MemWrite,
  output MemRad,
  output [1:0] Branch_X3b,
  output RegDest,
  output ALUsrc,
  output regDataSrc,
  output regWrite
);

  wire and_1_out, and_2_out, not_1_out, not_2_out, not_3_out, xnor_1_out;

  not not_1 (not_1_out, in_1[3]);
  not not_2 (not_2_out, in_1[1]);
  xnor xnor_1 (xnor_1_out, in_1[1], in_1[3]);
  and and_1 (and_1_out, not_1_out, in_1[2], not_2_out);
  and and_2 (and_2_out, in_1[0], in_1[3]);
  not not_3 (not_3_out, in_1[0]);
  Register_Control register_control_1 (
    .in_1(in_1), .RegData_ALU_1(regDataSrc), .REG_WRITE(regWrite), .ALUsrc_imd_1(RegDest),
    .RegDest_rt_1(ALUsrc));
  and and_3 (MemRad, in_1[0], and_1_out);
  and and_4 (MemWrite, and_1_out, not_3_out);
  nor nor_1 (Branch_X3b[0], in_1[2], xnor_1_out, and_2_out);

  assign Branch_X3b[1] = in_1[3];
endmodule

// Reg_ctrl
module Register_Control (
  input  [3:0] in_1,
  output ALUsrc_imd_1,
  output RegDest_rt_1,
  output RegData_ALU_1,
  output REG_WRITE
);

  wire and_1_out, and_2_out, and_3_out, and_4_out, and_5_out, and_6_out, and_7_out, nor_1_out, not_1_out,
       not_2_out, not_3_out, not_4_out;

  not not_1 (not_1_out, in_1[3]);
  not not_2 (not_2_out, in_1[0]);
  not not_3 (not_3_out, in_1[2]);
  not not_4 (not_4_out, in_1[1]);
  and and_1 (and_1_out, in_1[1], in_1[2]);
  nor nor_1 (nor_1_out, in_1[0], in_1[1]);
  and and_2 (and_2_out, in_1[1], not_2_out);
  and and_3 (and_3_out, not_4_out, not_3_out);
  and and_4 (and_4_out, in_1[3], in_1[2]);
  and and_5 (and_5_out, not_4_out, in_1[0]);
  and and_6 (and_6_out, in_1[3], in_1[1]);
  and and_7 (and_7_out, not_1_out, not_3_out, not_4_out);
  or or_1 (RegData_ALU_1, in_1[1], and_3_out, in_1[3]);
  or or_2 (REG_WRITE, and_1_out, and_4_out, and_5_out, and_6_out, and_7_out);
  Multiplexer #(.select(2)) multiplexer_1 (
    .in0(nor_1_out), .in1(1'b1), .in2(and_2_out), .in3(not_4_out), .out(ALUsrc_imd_1), .sel(in_1[3:2]),
    .en(1'b1));

  assign RegDest_rt_1 = ALUsrc_imd_1;
endmodule

// fwd
module fwd_ctrl (
  input  [3:0] rs,
  input  [3:0] EX_MEM_rd,
  input  [3:0] rt,
  input  [3:0] MEM_WB_rd,
  output Y1,
  output Y0,
  output X1,
  output X0
);

  wire nor_2_out, nor_4_out;
  wire [3:0] xor_1_out, xor_2_out, xor_3_out, xor_4_out;

  nor nor_1 (Y0, xor_1_out[3], xor_1_out[2], xor_1_out[1], xor_1_out[0]);
  or or_1 (Y1, Y0, nor_2_out);
  assign xor_1_out = rs ^ MEM_WB_rd;  // XOR_Gate xor_1, 4 bits wide
  nor nor_2 (nor_2_out, xor_2_out[3], xor_2_out[2], xor_2_out[1], xor_2_out[0]);
  assign xor_2_out = rs ^ EX_MEM_rd;  // XOR_Gate xor_2, 4 bits wide
  nor nor_3 (X0, xor_3_out[3], xor_3_out[2], xor_3_out[1], xor_3_out[0]);
  assign xor_3_out = rt ^ MEM_WB_rd;  // XOR_Gate xor_3, 4 bits wide
  or or_2 (X1, X0, nor_4_out);
  assign xor_4_out = rt ^ EX_MEM_rd;  // XOR_Gate xor_4, 4 bits wide
  nor nor_4 (nor_4_out, xor_4_out[3], xor_4_out[2], xor_4_out[1], xor_4_out[0]);
endmodule
