// Logisim project mips.circ as structural Verilog
module MIPS (
  input  in_1,
  output [3:0] out_2
);

  wire alu_mod_1_zero, ctrl_unit_1_alusrc, ctrl_unit_1_regdatasrc, ctrl_unit_1_regdest, ctrl_unit_1_regwrite,
       instruction_splitter_1_jump;
  wire [1:0] ctrl_unit_1_branch_x3b, ctrl_unit_1_memrad;
  wire [1:1] clock_1_out;
  wire [3:0] instruction_splitter_1_op_code, instruction_splitter_1_r_d, instruction_splitter_1_r_s,
       instruction_splitter_1_r_t, multiplexer_1_out;
  wire [7:0] alu_mod_1_result, instruction_splitter_1_immidiate, multiplexer_2_out, multiplexer_3_out,
       n8bit_8registor_1_busa, n8bit_8registor_1_busb, pc_unit_1_pc_out, ram_1_data, register_1_q;
  wire [19:0] rom_1_data;

  Clock clock_1 (.out(clock_1_out[1]));
  Register register_1 (.D(pc_unit_1_pc_out), .en(1'b1), .Q(register_1_q), .clk(clock_1_out[1]), .clr(in_1));
  PC_unit pc_unit_1 (
    .PC_in(register_1_q), .PC_out(pc_unit_1_pc_out), .jump_ammount(instruction_splitter_1_immidiate),
    .branch(ctrl_unit_1_branch_x3b[0]), .inequal(ctrl_unit_1_branch_x3b[1]), .zero(alu_mod_1_zero),
    .Jump(instruction_splitter_1_jump));
  ROM #(.dataWidth(20)) rom_1 (.addr(register_1_q), .data(rom_1_data), .sel(1'b1));
  Instruction_Splitter instruction_splitter_1 (
    .instruction(rom_1_data), .OP_code(instruction_splitter_1_op_code), .R_s(instruction_splitter_1_r_s),
    .R_t(instruction_splitter_1_r_t), .R_d(instruction_splitter_1_r_d),
    .Immidiate(instruction_splitter_1_immidiate), .Jump(instruction_splitter_1_jump));
  ctrl_unit ctrl_unit_1 (
    .in_1(instruction_splitter_1_op_code), .Branch_X3b(ctrl_unit_1_branch_x3b),
    .regWrite(ctrl_unit_1_regwrite), .regDataSrc(ctrl_unit_1_regdatasrc), .MemRad(ctrl_unit_1_memrad[0]),
    .MemWrite(ctrl_unit_1_memrad[1]), .RegDest(ctrl_unit_1_regdest), .ALUsrc(ctrl_unit_1_alusrc));
  Multiplexer #(.width(4)) multiplexer_1 (
    .in0(instruction_splitter_1_r_d), .in1(instruction_splitter_1_r_t), .out(multiplexer_1_out),
    .sel(ctrl_unit_1_regdest), .en(1'b1));
  _8bit_8Registor u_8bit_8registor_1 (
    .WriteEnable(ctrl_unit_1_regwrite), .Data(multiplexer_3_out), .Clock(clock_1_out[1]),
    .BusA(n8bit_8registor_1_busa), .BusB(n8bit_8registor_1_busb), .RegD(multiplexer_1_out),
    .RegB(instruction_splitter_1_r_t), .RegA(instruction_splitter_1_r_s), .Reset(in_1));
  ALU_ctrl alu_ctrl_1 (.in_1(instruction_splitter_1_op_code), .out_2(out_2));
  ALU_mod alu_mod_1 (
    .A(n8bit_8registor_1_busa), .B(multiplexer_2_out), .Zero(alu_mod_1_zero), .Result(alu_mod_1_result),
    .in_3(out_2));  // open: OverFlow
  Multiplexer #(.width(8)) multiplexer_2 (
    .in0(n8bit_8registor_1_busb), .in1(instruction_splitter_1_immidiate), .out(multiplexer_2_out),
    .sel(ctrl_unit_1_alusrc), .en(1'b1));
  RAM #(.bus("separate")) ram_1 (
    .addr(alu_mod_1_result), .din(n8bit_8registor_1_busb), .data(ram_1_data), .str(ctrl_unit_1_memrad[1]),
    .sel(1'b1), .clk(clock_1_out[1]), .ld(ctrl_unit_1_memrad[0]), .clr(in_1));
  Multiplexer #(.width(8)) multiplexer_3 (
    .in0(ram_1_data), .in1(alu_mod_1_result), .out(multiplexer_3_out), .sel(ctrl_unit_1_regdatasrc), .en(1'b1));

  // Notes on the sheet:
  //   contents of rom_1 (hex, n*v repeats v):
  //   606ff 60700 60178 60278 f2110
endmodule

module component_test (
  input  [7:0] in_1,
  input  [7:0] in_2,
  input  [3:0] in_3,
  output out_4,
  output [7:0] out_5,
  output out_6
);

  ALU_mod alu_mod_1 (.A(in_1), .B(in_2), .Zero(out_4), .Result(out_5), .OverFlow(out_6), .in_3(in_3));
endmodule

// PC ctrl
module PC_unit (
  input  [7:0] PC_in,
  input  Jump,
  input  branch,
  input  inequal,
  input  zero,
  input  [7:0] jump_ammount,
  output [7:0] PC_out
);

  wire xor_1_out;
  wire [0:0] and_1_out;
  wire [7:0] adder_1_out, adder_2_out;

  Adder adder_1 (.a(PC_in), .b(8'h1), .out(adder_1_out), .cin(1'b0));  // open: cout
  Adder adder_2 (.a(adder_1_out), .b(jump_ammount), .out(adder_2_out), .cin(1'b0));  // open: cout
  Multiplexer #(.select(2), .width(8)) multiplexer_1 (
    .in0(adder_1_out), .in1(adder_2_out), .in2(jump_ammount), .in3(jump_ammount), .out(PC_out),
    .sel({Jump, and_1_out[0]}), .en(1'b1));
  and and_1 (and_1_out[0], branch, xor_1_out);
  xor xor_1 (xor_1_out, inequal, zero);
endmodule
