// Logisim project pipeline_components.circ as structural Verilog
module ID (
  input  [19:0] in_1,
  input  in_2,
  input  clock,
  input  [7:0] Register_Data_In,
  input  [3:0] Data_Destiantion_Rd,
  input  Reset,
  output [1:0] branch_ne_b,
  output J,
  output MemRead,
  output MemWrite,
  output ALU_src,
  output Reg_Src__ALU_1,
  output RegWrite,
  output [3:0] Rd,
  output [3:0] Rt,
  output [3:0] Rs,
  output [7:0] Rs_Value,
  output [7:0] Rt_Value,
  output [7:0] Im,
  output [3:0] ALU_Op
);

  wire ctrl_unit_1_regdest, not_1_out;
  wire [3:0] instruction_splitter_1_op_code, instruction_splitter_1_r_d;

  not not_1 (not_1_out, clock);
  Instruction_Splitter instruction_splitter_1 (
    .instruction(in_1), .OP_code(instruction_splitter_1_op_code), .R_s(Rs), .R_t(Rt),
    .R_d(instruction_splitter_1_r_d), .Immidiate(Im), .Jump(J));
  ctrl_unit ctrl_unit_1 (
    .in_1(instruction_splitter_1_op_code), .Branch_X3b(branch_ne_b), .regWrite(RegWrite),
    .regDataSrc(Reg_Src__ALU_1), .MemRad(MemRead), .MemWrite(MemWrite), .RegDest(ctrl_unit_1_regdest),
    .ALUsrc(ALU_src));
  Multiplexer #(.width(4)) multiplexer_1 (
    .in0(instruction_splitter_1_r_d), .in1(Rt), .out(Rd), .sel(ctrl_unit_1_regdest), .en(1'b1));
  _8bit_8Registor u_8bit_8registor_1 (
    .WriteEnable(in_2), .Data(Register_Data_In), .Clock(not_1_out), .BusA(Rs_Value), .BusB(Rt_Value),
    .RegD(Data_Destiantion_Rd), .RegB(Rt), .RegA(Rs), .Reset(Reset));
  ALU_ctrl alu_ctrl_1 (.in_1(instruction_splitter_1_op_code), .out_2(ALU_Op));
endmodule
