// Logisim project pipeline_registers.circ as structural Verilog
// IF ID
module IF_ID (
  input  control,
  input  [7:0] Next_PC,
  input  [19:0] Instruction,
  input  Reset,
  input  clock,
  output [7:0] Next_PC_2,
  output [19:0] Instruction_out
);

  Register #(.width(28)) register_1 (
    .D({Instruction, Next_PC}), .en(control), .Q({Instruction_out, Next_PC_2}), .clk(clock), .clr(Reset));
endmodule
